// Logisim project schematic.circ as structural Verilog: 17 circuits, main circuit main
// div_low
module main (
  input  clk,
  input  rst,
  input  Jen,
  input  [31:0] Jin,
  output instDone0,
  output instDone1,
  output [31:0] R1_0,
  output [31:0] R1_1,
  output [31:0] R2_0,
  output [31:0] R2_1,
  output [31:0] R3_0,
  output [31:0] R3_1,
  output [31:0] R4_0,
  output [31:0] R4_1,
  output [31:0] R5_0,
  output [31:0] Jout,
  output [31:0] R5_1,
  output [31:0] R6_0,
  output [31:0] R6_1,
  output [31:0] R7_0,
  output [31:0] R7_1,
  output [31:0] R8_0,
  output [31:0] R8_1,
  output [31:0] R9_0,
  output [31:0] R9_1,
  output [31:0] R10_0,
  output [31:0] R10_1,
  output [31:0] R11_0,
  output [31:0] R11_1,
  output [31:0] R12_0,
  output [31:0] R12_1,
  output [31:0] R13_0,
  output [31:0] R13_1,
  output [31:0] R14_0,
  output [31:0] R14_1,
  output [31:0] R15_0,
  output [31:0] R15_1,
  output [31:0] R16_0,
  output [31:0] R16_1,
  output [31:0] R17_0,
  output [31:0] R17_1,
  output [31:0] R18_0,
  output [31:0] R18_1,
  output [31:0] R19_0,
  output [31:0] R19_1,
  output [31:0] R20_0,
  output [31:0] R20_1,
  output [31:0] R21_0,
  output [31:0] R21_1,
  output [31:0] R22_0,
  output [31:0] R22_1,
  output [31:0] R23_0,
  output [31:0] R23_1,
  output [31:0] R24_0,
  output [31:0] R24_1,
  output [31:0] R25_0,
  output [31:0] R25_1,
  output [31:0] R26_0,
  output [31:0] R26_1,
  output [31:0] R27_0,
  output [31:0] R27_1,
  output [31:0] R28_0,
  output [31:0] R28_1,
  output [31:0] R29_0,
  output [31:0] R29_1,
  output [31:0] R30_0,
  output [31:0] R30_1,
  output [31:0] R31_0,
  output [31:0] R31_1,
  output [4:0] state0,
  output [4:0] state1
);

  wire and_1_out, and_2_out, and_3_out, and_4_out, and_5_out, d_ff_1_q, d_ff_2_q, en, ex0, ex1, nand_1_out,
       not_1_out, not_2_out, or_1_out, syns0, syns1, wen0, wen1;
  wire [8:0] addr0, addr1, cpu0_address, cpu1_address, multiplexer_5_out, multiplexer_6_out,
       multiplexer_7_out, multiplexer_8_out, pc0, pc1, register_2_q, register_4_q;
  wire [31:0] bit_extender_1_out, bit_extender_2_out, data0, data1, DataMem, I_cache0_dout, I_cache0_jout,
       I_cache1_dout, I_cache1_jout, multiplexer_1_out, multiplexer_2_out, multiplexer_3_out,
       multiplexer_4_out, register_1_q, register_3_q;
  wire [31:9] srlshift_1_out1, srlshift_2_out1;

  not not_1 (not_1_out, ex0);
  nand nand_1 (nand_1_out, not_1_out, ex1);
  and and_1 (and_1_out, clk, nand_1_out);
  jtag_ram512 I_cache0 (
    .clk(clk), .Jen(Jen), .Jin(Jin), .Addr(pc0), .Jout(I_cache0_jout), .Dout(I_cache0_dout));  // open: Din, Wen
  Multiplexer #(.width(32)) multiplexer_1 (.in0(DataMem), .in1(multiplexer_1_out), .out(multiplexer_1_out), .sel(clk));
  cpu cpu0 (
    .clk(and_1_out), .rst(rst), .syns_in(syns1), .Dout(I_cache0_dout), .cpu_id(1'b0),
    .DataMem(multiplexer_1_out), .InstDone(instDone0), .mem_write(wen0), .PC_out(pc0), .syns_out(syns0),
    .exchange(ex0), .R1(R1_0), .R2(R2_0), .R3(R3_0), .R4(R4_0), .R5(R5_0), .R6(R6_0), .R7(R7_0), .R8(R8_0),
    .R9(R9_0), .WriteData(data0), .R10(R10_0), .R11(R11_0), .R12(R12_0), .R13(R13_0), .R14(R14_0),
    .R15(R15_0), .R16(R16_0), .address(cpu0_address), .R17(R17_0), .R18(R18_0), .R19(R19_0), .R20(R20_0),
    .R21(R21_0), .R22(R22_0), .R23(R23_0), .R24(R24_0), .R25(R25_0), .R26(R26_0), .R27(R27_0), .R28(R28_0),
    .R29(R29_0), .R30(R30_0), .R31(R31_0), .state(state0));  // open: aluDone
  assign bit_extender_1_out = {{23{1'b0}}, cpu0_address};  // Bit_Extender bit_extender_1
  srlShift srlshift_1 (.in1(bit_extender_1_out), .shift(5'b00010), .out1({srlshift_1_out1, addr0}));
  and and_2 (and_2_out, clk, not_2_out);
  not not_2 (not_2_out, ex0);
  jtag_ram512 I_cache1 (
    .clk(clk), .Jen(Jen), .Jin(Jin), .Addr(pc1), .Jout(I_cache1_jout), .Dout(I_cache1_dout));  // open: Din, Wen
  Multiplexer #(.width(32)) multiplexer_2 (.in0(multiplexer_2_out), .in1(DataMem), .out(multiplexer_2_out), .sel(clk));
  cpu cpu1 (
    .clk(and_2_out), .rst(rst), .syns_in(syns0), .Dout(I_cache1_dout), .cpu_id(1'b1),
    .DataMem(multiplexer_2_out), .InstDone(instDone1), .mem_write(wen1), .PC_out(pc1), .syns_out(syns1),
    .exchange(ex1), .R1(R1_1), .R2(R2_1), .R3(R3_1), .R4(R4_1), .R5(R5_1), .R6(R6_1), .R7(R7_1), .R8(R8_1),
    .R9(R9_1), .WriteData(data1), .R10(R10_1), .R11(R11_1), .R12(R12_1), .R13(R13_1), .R14(R14_1),
    .R15(R15_1), .R16(R16_1), .address(cpu1_address), .R17(R17_1), .R18(R18_1), .R19(R19_1), .R20(R20_1),
    .R21(R21_1), .R22(R22_1), .R23(R23_1), .R24(R24_1), .R25(R25_1), .R26(R26_1), .R27(R27_1), .R28(R28_1),
    .R29(R29_1), .R30(R30_1), .R31(R31_1), .state(state1));  // open: aluDone
  assign bit_extender_2_out = {{23{1'b0}}, cpu1_address};  // Bit_Extender bit_extender_2
  srlShift srlshift_2 (.in1(bit_extender_2_out), .shift(5'b00010), .out1({srlshift_2_out1, addr1}));
  and and_3 (and_3_out, wen0, wen1);
  Register #(.width(32)) register_1 (.D(data1), .en(and_3_out), .clk(clk), .Q(register_1_q), .clr(rst));
  and and_4 (and_4_out, wen0, wen1);
  D_Flip_Flop d_ff_1 (.D(wen0), .clk(clk), .Q(d_ff_1_q), .reset(rst));  // open: Qn, preset
  D_Flip_Flop d_ff_2 (.D(wen1), .clk(clk), .Q(d_ff_2_q), .reset(rst));  // open: Qn, preset
  Register #(.width(9)) register_2 (.D(addr1), .en(and_4_out), .clk(clk), .Q(register_2_q), .clr(rst));
  Multiplexer #(.width(32)) multiplexer_3 (.in0(register_1_q), .in1(data1), .out(multiplexer_3_out), .sel(wen1));
  and and_5 (and_5_out, d_ff_1_q, d_ff_2_q);
  Multiplexer #(.width(32)) multiplexer_4 (.in0(multiplexer_3_out), .in1(data0), .out(multiplexer_4_out), .sel(wen0));
  Multiplexer #(.width(9)) multiplexer_5 (.in0(register_2_q), .in1(addr1), .out(multiplexer_5_out), .sel(wen1));
  Register #(.width(32)) register_3 (.D(multiplexer_4_out), .en(1'b1), .clk(clk), .Q(register_3_q), .clr(rst));
  or or_1 (or_1_out, wen0, wen1, and_5_out);
  Multiplexer #(.width(9)) multiplexer_6 (.in0(multiplexer_5_out), .in1(addr0), .out(multiplexer_6_out), .sel(wen0));
  D_Flip_Flop d_ff_3 (.D(or_1_out), .clk(clk), .Q(en), .reset(rst));  // open: Qn, preset
  Multiplexer #(.width(9)) multiplexer_7 (.in0(addr0), .in1(addr1), .out(multiplexer_7_out), .sel(clk));
  Register #(.width(9)) register_4 (.D(multiplexer_6_out), .en(1'b1), .clk(clk), .Q(register_4_q), .clr(rst));
  Multiplexer #(.width(9)) multiplexer_8 (
    .in0(multiplexer_7_out), .in1(register_4_q), .out(multiplexer_8_out), .sel(en));
  jtag_ram512 D_cache (
    .clk(clk), .Jen(Jen), .Din(register_3_q), .Wen(en), .Addr(multiplexer_8_out), .Jout(Jout), .Dout(DataMem));  // open: Jin
endmodule

module jtag_ram8 (
  input  clk,
  input  Jen,
  input  [31:0] Din,
  input  [31:0] Jin,
  input  Wen,
  input  [2:0] Addr,
  output [31:0] Dout,
  output [31:0] Jout
);

  wire decoder_1_out0, decoder_1_out1, decoder_1_out2, decoder_1_out3, decoder_1_out4, decoder_1_out5,
       decoder_1_out6, decoder_1_out7, or_1_out, or_2_out, or_3_out, or_4_out, or_5_out, or_6_out, or_7_out,
       or_8_out;
  wire [31:0] M0, M1, M2, M3, M4, M5, M6, multiplexer_1_out, multiplexer_2_out, multiplexer_3_out,
       multiplexer_4_out, multiplexer_5_out, multiplexer_6_out, multiplexer_7_out, multiplexer_8_out;

  Decoder #(.select(3)) decoder_1 (
    .out0(decoder_1_out0), .out1(decoder_1_out1), .out2(decoder_1_out2), .out3(decoder_1_out3),
    .out4(decoder_1_out4), .out5(decoder_1_out5), .out6(decoder_1_out6), .out7(decoder_1_out7), .sel(Addr),
    .en(Wen));
  Multiplexer #(.width(32)) multiplexer_1 (.in0(Din), .in1(Jin), .out(multiplexer_1_out), .sel(Jen));
  Multiplexer #(.width(32)) multiplexer_2 (.in0(Din), .in1(M0), .out(multiplexer_2_out), .sel(Jen));
  Multiplexer #(.width(32)) multiplexer_3 (.in0(Din), .in1(M1), .out(multiplexer_3_out), .sel(Jen));
  Multiplexer #(.width(32)) multiplexer_4 (.in0(Din), .in1(M2), .out(multiplexer_4_out), .sel(Jen));
  Multiplexer #(.width(32)) multiplexer_5 (.in0(Din), .in1(M3), .out(multiplexer_5_out), .sel(Jen));
  Multiplexer #(.width(32)) multiplexer_6 (.in0(Din), .in1(M4), .out(multiplexer_6_out), .sel(Jen));
  Multiplexer #(.width(32)) multiplexer_7 (.in0(Din), .in1(M5), .out(multiplexer_7_out), .sel(Jen));
  Multiplexer #(.width(32)) multiplexer_8 (.in0(Din), .in1(M6), .out(multiplexer_8_out), .sel(Jen));
  Register #(.width(32)) register_1 (.D(multiplexer_1_out), .en(or_1_out), .clk(clk), .Q(M0));  // open: clr
  or or_1 (or_1_out, Jen, decoder_1_out0);
  Register #(.width(32)) register_2 (.D(multiplexer_2_out), .en(or_2_out), .clk(clk), .Q(M1));  // open: clr
  or or_2 (or_2_out, Jen, decoder_1_out1);
  Register #(.width(32)) register_3 (.D(multiplexer_3_out), .en(or_3_out), .clk(clk), .Q(M2));  // open: clr
  or or_3 (or_3_out, Jen, decoder_1_out2);
  Register #(.width(32)) register_4 (.D(multiplexer_4_out), .en(or_4_out), .clk(clk), .Q(M3));  // open: clr
  or or_4 (or_4_out, Jen, decoder_1_out3);
  Register #(.width(32)) register_5 (.D(multiplexer_5_out), .en(or_5_out), .clk(clk), .Q(M4));  // open: clr
  or or_5 (or_5_out, Jen, decoder_1_out4);
  Register #(.width(32)) register_6 (.D(multiplexer_6_out), .en(or_6_out), .clk(clk), .Q(M5));  // open: clr
  or or_6 (or_6_out, Jen, decoder_1_out5);
  Register #(.width(32)) register_7 (.D(multiplexer_7_out), .en(or_7_out), .clk(clk), .Q(M6));  // open: clr
  or or_7 (or_7_out, Jen, decoder_1_out6);
  Register #(.width(32)) register_8 (.D(multiplexer_8_out), .en(or_8_out), .clk(clk), .Q(Jout));  // open: clr
  or or_8 (or_8_out, Jen, decoder_1_out7);
  Multiplexer #(.select(3), .width(32)) multiplexer_9 (
    .in0(M0), .in1(M1), .in2(M2), .in3(M3), .in4(M4), .in5(M5), .in6(M6), .in7(Jout), .out(Dout), .sel(Addr));

  // Other names for the same wires on the sheet: M7[31:0] = Jout
endmodule

module jtag_ram64 (
  input  clk,
  input  Jen,
  input  [31:0] Din,
  input  [31:0] Jin,
  input  Wen,
  input  [5:0] Addr,
  output [31:0] Dout,
  output [31:0] Jout
);

  wire decoder_1_out0, decoder_1_out1, decoder_1_out2, decoder_1_out3, decoder_1_out4, decoder_1_out5,
       decoder_1_out6, decoder_1_out7;
  wire [31:0] b0_dout, b0_jout, b1_dout, b1_jout, b2_dout, b2_jout, b3_dout, b3_jout, b4_dout, b4_jout,
       b5_dout, b5_jout, b6_dout, b6_jout, b7_dout;

  Decoder #(.select(3)) decoder_1 (
    .out0(decoder_1_out0), .out1(decoder_1_out1), .out2(decoder_1_out2), .out3(decoder_1_out3),
    .out4(decoder_1_out4), .out5(decoder_1_out5), .out6(decoder_1_out6), .out7(decoder_1_out7),
    .sel(Addr[5:3]), .en(Wen));
  jtag_ram8 b0 (
    .clk(clk), .Jen(Jen), .Din(Din), .Jin(Jin), .Wen(decoder_1_out0), .Addr(Addr[2:0]), .Dout(b0_dout),
    .Jout(b0_jout));
  jtag_ram8 b1 (
    .clk(clk), .Jen(Jen), .Din(Din), .Jin(b0_jout), .Wen(decoder_1_out1), .Addr(Addr[2:0]), .Dout(b1_dout),
    .Jout(b1_jout));
  jtag_ram8 b2 (
    .clk(clk), .Jen(Jen), .Din(Din), .Jin(b1_jout), .Wen(decoder_1_out2), .Addr(Addr[2:0]), .Dout(b2_dout),
    .Jout(b2_jout));
  jtag_ram8 b3 (
    .clk(clk), .Jen(Jen), .Din(Din), .Jin(b2_jout), .Wen(decoder_1_out3), .Addr(Addr[2:0]), .Dout(b3_dout),
    .Jout(b3_jout));
  jtag_ram8 b4 (
    .clk(clk), .Jen(Jen), .Din(Din), .Jin(b3_jout), .Wen(decoder_1_out4), .Addr(Addr[2:0]), .Dout(b4_dout),
    .Jout(b4_jout));
  jtag_ram8 b5 (
    .clk(clk), .Jen(Jen), .Din(Din), .Jin(b4_jout), .Wen(decoder_1_out5), .Addr(Addr[2:0]), .Dout(b5_dout),
    .Jout(b5_jout));
  jtag_ram8 b6 (
    .clk(clk), .Jen(Jen), .Din(Din), .Jin(b5_jout), .Wen(decoder_1_out6), .Addr(Addr[2:0]), .Dout(b6_dout),
    .Jout(b6_jout));
  jtag_ram8 b7 (
    .clk(clk), .Jen(Jen), .Din(Din), .Jin(b6_jout), .Wen(decoder_1_out7), .Addr(Addr[2:0]), .Dout(b7_dout),
    .Jout(Jout));
  Multiplexer #(.select(3), .width(32)) multiplexer_1 (
    .in0(b0_dout), .in1(b1_dout), .in2(b2_dout), .in3(b3_dout), .in4(b4_dout), .in5(b5_dout), .in6(b6_dout),
    .in7(b7_dout), .out(Dout), .sel(Addr[5:3]));
endmodule

module jtag_ram512 (
  input  clk,
  input  Jen,
  input  [31:0] Din,
  input  [31:0] Jin,
  input  Wen,
  input  [8:0] Addr,
  output [31:0] Jout,
  output [31:0] Dout
);

  wire decoder_1_out0, decoder_1_out1, decoder_1_out2, decoder_1_out3, decoder_1_out4, decoder_1_out5,
       decoder_1_out6, decoder_1_out7;
  wire [31:0] b0_dout, b0_jout, b1_dout, b1_jout, b2_dout, b2_jout, b3_dout, b3_jout, b4_dout, b4_jout,
       b5_dout, b5_jout, b6_dout, b6_jout, b7_dout;

  Decoder #(.select(3)) decoder_1 (
    .out0(decoder_1_out0), .out1(decoder_1_out1), .out2(decoder_1_out2), .out3(decoder_1_out3),
    .out4(decoder_1_out4), .out5(decoder_1_out5), .out6(decoder_1_out6), .out7(decoder_1_out7),
    .sel(Addr[8:6]), .en(Wen));
  jtag_ram64 b0 (
    .clk(clk), .Jen(Jen), .Din(Din), .Jin(Jin), .Wen(decoder_1_out0), .Addr(Addr[5:0]), .Dout(b0_dout),
    .Jout(b0_jout));
  jtag_ram64 b1 (
    .clk(clk), .Jen(Jen), .Din(Din), .Jin(b0_jout), .Wen(decoder_1_out1), .Addr(Addr[5:0]), .Dout(b1_dout),
    .Jout(b1_jout));
  jtag_ram64 b2 (
    .clk(clk), .Jen(Jen), .Din(Din), .Jin(b1_jout), .Wen(decoder_1_out2), .Addr(Addr[5:0]), .Dout(b2_dout),
    .Jout(b2_jout));
  jtag_ram64 b3 (
    .clk(clk), .Jen(Jen), .Din(Din), .Jin(b2_jout), .Wen(decoder_1_out3), .Addr(Addr[5:0]), .Dout(b3_dout),
    .Jout(b3_jout));
  jtag_ram64 b4 (
    .clk(clk), .Jen(Jen), .Din(Din), .Jin(b3_jout), .Wen(decoder_1_out4), .Addr(Addr[5:0]), .Dout(b4_dout),
    .Jout(b4_jout));
  jtag_ram64 b5 (
    .clk(clk), .Jen(Jen), .Din(Din), .Jin(b4_jout), .Wen(decoder_1_out5), .Addr(Addr[5:0]), .Dout(b5_dout),
    .Jout(b5_jout));
  jtag_ram64 b6 (
    .clk(clk), .Jen(Jen), .Din(Din), .Jin(b5_jout), .Wen(decoder_1_out6), .Addr(Addr[5:0]), .Dout(b6_dout),
    .Jout(b6_jout));
  jtag_ram64 b7 (
    .clk(clk), .Jen(Jen), .Din(Din), .Jin(b6_jout), .Wen(decoder_1_out7), .Addr(Addr[5:0]), .Dout(b7_dout),
    .Jout(Jout));
  Multiplexer #(.select(3), .width(32)) multiplexer_1 (
    .in0(b0_dout), .in1(b1_dout), .in2(b2_dout), .in3(b3_dout), .in4(b4_dout), .in5(b5_dout), .in6(b6_dout),
    .in7(b7_dout), .out(Dout), .sel(Addr[8:6]));
endmodule

module regfile (
  input  clk,
  input  rst,
  input  [31:0] Dwrite,
  input  [4:0] Awrite,
  input  [4:0] Aread0,
  input  [4:0] Aread1,
  output [31:0] Dread0,
  output [31:0] Dread1,
  output [31:0] R1,
  output [31:0] R2,
  output [31:0] R3,
  output [31:0] R4,
  output [31:0] R5,
  output [31:0] R6,
  output [31:0] R7,
  output [31:0] R8,
  output [31:0] R9,
  output [31:0] R10,
  output [31:0] R11,
  output [31:0] R12,
  output [31:0] R13,
  output [31:0] R14,
  output [31:0] R15,
  output [31:0] R16,
  output [31:0] R17,
  output [31:0] R18,
  output [31:0] R19,
  output [31:0] R20,
  output [31:0] R21,
  output [31:0] R22,
  output [31:0] R23,
  output [31:0] R24,
  output [31:0] R25,
  output [31:0] R26,
  output [31:0] R27,
  output [31:0] R28,
  output [31:0] R29,
  output [31:0] R30,
  output [31:0] R31
);

  wire and_1_out, and_2_out, and_3_out, and_4_out, and_5_out, and_6_out, and_7_out, and_8_out, and_9_out,
       and_10_out, and_11_out, and_12_out, and_13_out, and_14_out, and_15_out, and_16_out, and_17_out,
       and_18_out, and_19_out, and_20_out, and_21_out, and_22_out, and_23_out, and_24_out, and_25_out,
       and_26_out, and_27_out, and_28_out, and_29_out, and_30_out, and_31_out, and_32_out, decoder_1_out0,
       decoder_1_out1, decoder_1_out2, decoder_1_out3, decoder_1_out4, decoder_1_out5, decoder_1_out6,
       decoder_1_out7, decoder_2_out0, decoder_2_out1, decoder_2_out2, decoder_2_out3, or_1_out, or_2_out,
       or_3_out, or_4_out, or_5_out, or_6_out, or_7_out, or_8_out, or_9_out, or_10_out, or_11_out, or_12_out,
       or_13_out, or_14_out, or_15_out, or_16_out, or_17_out, or_18_out, or_19_out, or_20_out, or_21_out,
       or_22_out, or_23_out, or_24_out, or_25_out, or_26_out, or_27_out, or_28_out, or_29_out, or_30_out,
       or_31_out, or_32_out, undriven_2, undriven_3, undriven_4, undriven_5;
  wire [31:0] multiplexer_1_out, multiplexer_2_out, multiplexer_3_out, multiplexer_4_out, multiplexer_5_out,
       multiplexer_6_out, multiplexer_7_out, multiplexer_8_out, multiplexer_9_out, undriven;

  Register #(.width(32)) register_1 (.D(undriven), .en(or_1_out), .clk(undriven_2));  // open: Q, clr
  or or_1 (or_1_out, undriven_5, and_1_out);
  and and_1 (and_1_out, undriven_4, undriven_3);
  Decoder #(.select(3)) decoder_1 (
    .out0(decoder_1_out0), .out1(decoder_1_out1), .out2(decoder_1_out2), .out3(decoder_1_out3),
    .out4(decoder_1_out4), .out5(decoder_1_out5), .out6(decoder_1_out6), .out7(decoder_1_out7),
    .sel(Awrite[4:2]));  // open: en
  Decoder #(.select(2)) decoder_2 (
    .out0(decoder_2_out0), .out1(decoder_2_out1), .out2(decoder_2_out2), .out3(decoder_2_out3),
    .sel(Awrite[1:0]));  // open: en
  Multiplexer #(.width(32)) multiplexer_1 (.in0(Dwrite), .in1({32{1'b0}}), .out(multiplexer_1_out), .sel(rst));
  and and_2 (and_2_out, decoder_2_out0, decoder_1_out1);
  and and_3 (and_3_out, decoder_2_out0, decoder_1_out2);
  and and_4 (and_4_out, decoder_2_out0, decoder_1_out3);
  and and_5 (and_5_out, decoder_2_out0, decoder_1_out4);
  and and_6 (and_6_out, decoder_2_out0, decoder_1_out5);
  and and_7 (and_7_out, decoder_2_out0, decoder_1_out6);
  and and_8 (and_8_out, decoder_2_out0, decoder_1_out7);
  Register #(.width(32)) register_2 (.D(multiplexer_1_out), .en(or_2_out), .clk(clk), .Q(R4));  // open: clr
  or or_2 (or_2_out, rst, and_2_out);
  Register #(.width(32)) register_3 (.D(multiplexer_1_out), .en(or_3_out), .clk(clk), .Q(R8));  // open: clr
  or or_3 (or_3_out, rst, and_3_out);
  Register #(.width(32)) register_4 (.D(multiplexer_1_out), .en(or_4_out), .clk(clk), .Q(R12));  // open: clr
  or or_4 (or_4_out, rst, and_4_out);
  Register #(.width(32)) register_5 (.D(multiplexer_1_out), .en(or_5_out), .clk(clk), .Q(R16));  // open: clr
  or or_5 (or_5_out, rst, and_5_out);
  Register #(.width(32)) register_6 (.D(multiplexer_1_out), .en(or_6_out), .clk(clk), .Q(R20));  // open: clr
  or or_6 (or_6_out, rst, and_6_out);
  Register #(.width(32)) register_7 (.D(multiplexer_1_out), .en(or_7_out), .clk(clk), .Q(R24));  // open: clr
  or or_7 (or_7_out, rst, and_7_out);
  Register #(.width(32)) register_8 (.D(multiplexer_1_out), .en(or_8_out), .clk(clk), .Q(R28));  // open: clr
  or or_8 (or_8_out, rst, and_8_out);
  Multiplexer #(.select(3), .width(32)) multiplexer_2 (
    .in0({32{1'b0}}), .in1(R4), .in2(R8), .in3(R12), .in4(R16), .in5(R20), .in6(R24), .in7(R28),
    .out(multiplexer_2_out), .sel(Aread0[4:2]));
  Multiplexer #(.select(3), .width(32)) multiplexer_3 (
    .in0({32{1'b0}}), .in1(R4), .in2(R8), .in3(R12), .in4(R16), .in5(R20), .in6(R24), .in7(R28),
    .out(multiplexer_3_out), .sel(Aread1[4:2]));
  and and_9 (and_9_out, decoder_2_out1, decoder_1_out0);
  and and_10 (and_10_out, decoder_2_out1, decoder_1_out1);
  and and_11 (and_11_out, decoder_2_out1, decoder_1_out2);
  and and_12 (and_12_out, decoder_2_out1, decoder_1_out3);
  and and_13 (and_13_out, decoder_2_out1, decoder_1_out4);
  and and_14 (and_14_out, decoder_2_out1, decoder_1_out5);
  and and_15 (and_15_out, decoder_2_out1, decoder_1_out6);
  and and_16 (and_16_out, decoder_2_out1, decoder_1_out7);
  Register #(.width(32)) register_9 (.D(multiplexer_1_out), .en(or_9_out), .clk(clk), .Q(R1));  // open: clr
  or or_9 (or_9_out, rst, and_9_out);
  Register #(.width(32)) register_10 (.D(multiplexer_1_out), .en(or_10_out), .clk(clk), .Q(R5));  // open: clr
  or or_10 (or_10_out, rst, and_10_out);
  Register #(.width(32)) register_11 (.D(multiplexer_1_out), .en(or_11_out), .clk(clk), .Q(R9));  // open: clr
  or or_11 (or_11_out, rst, and_11_out);
  Register #(.width(32)) register_12 (.D(multiplexer_1_out), .en(or_12_out), .clk(clk), .Q(R13));  // open: clr
  or or_12 (or_12_out, rst, and_12_out);
  Register #(.width(32)) register_13 (.D(multiplexer_1_out), .en(or_13_out), .clk(clk), .Q(R17));  // open: clr
  or or_13 (or_13_out, rst, and_13_out);
  Register #(.width(32)) register_14 (.D(multiplexer_1_out), .en(or_14_out), .clk(clk), .Q(R21));  // open: clr
  or or_14 (or_14_out, rst, and_14_out);
  Register #(.width(32)) register_15 (.D(multiplexer_1_out), .en(or_15_out), .clk(clk), .Q(R25));  // open: clr
  or or_15 (or_15_out, rst, and_15_out);
  Register #(.width(32)) register_16 (.D(multiplexer_1_out), .en(or_16_out), .clk(clk), .Q(R29));  // open: clr
  or or_16 (or_16_out, rst, and_16_out);
  Multiplexer #(.select(3), .width(32)) multiplexer_4 (
    .in0(R1), .in1(R5), .in2(R9), .in3(R13), .in4(R17), .in5(R21), .in6(R25), .in7(R29),
    .out(multiplexer_4_out), .sel(Aread0[4:2]));
  Multiplexer #(.select(3), .width(32)) multiplexer_5 (
    .in0(R1), .in1(R5), .in2(R9), .in3(R13), .in4(R17), .in5(R21), .in6(R25), .in7(R29),
    .out(multiplexer_5_out), .sel(Aread1[4:2]));
  Register #(.width(32)) register_17 (.D(multiplexer_1_out), .en(or_17_out), .clk(clk), .Q(R2));  // open: clr
  or or_17 (or_17_out, rst, and_17_out);
  and and_17 (and_17_out, decoder_2_out2, decoder_1_out0);
  Register #(.width(32)) register_18 (.D(multiplexer_1_out), .en(or_18_out), .clk(clk), .Q(R6));  // open: clr
  or or_18 (or_18_out, rst, and_18_out);
  and and_18 (and_18_out, decoder_2_out2, decoder_1_out1);
  Register #(.width(32)) register_19 (.D(multiplexer_1_out), .en(or_19_out), .clk(clk), .Q(R10));  // open: clr
  or or_19 (or_19_out, rst, and_19_out);
  and and_19 (and_19_out, decoder_2_out2, decoder_1_out2);
  Register #(.width(32)) register_20 (.D(multiplexer_1_out), .en(or_20_out), .clk(clk), .Q(R14));  // open: clr
  or or_20 (or_20_out, rst, and_20_out);
  and and_20 (and_20_out, decoder_2_out2, decoder_1_out3);
  Register #(.width(32)) register_21 (.D(multiplexer_1_out), .en(or_21_out), .clk(clk), .Q(R18));  // open: clr
  or or_21 (or_21_out, rst, and_21_out);
  and and_21 (and_21_out, decoder_2_out2, decoder_1_out4);
  Register #(.width(32)) register_22 (.D(multiplexer_1_out), .en(or_22_out), .clk(clk), .Q(R22));  // open: clr
  or or_22 (or_22_out, rst, and_22_out);
  and and_22 (and_22_out, decoder_2_out2, decoder_1_out5);
  Register #(.width(32)) register_23 (.D(multiplexer_1_out), .en(or_23_out), .clk(clk), .Q(R26));  // open: clr
  or or_23 (or_23_out, rst, and_23_out);
  and and_23 (and_23_out, decoder_2_out2, decoder_1_out6);
  Register #(.width(32)) register_24 (.D(multiplexer_1_out), .en(or_24_out), .clk(clk), .Q(R30));  // open: clr
  or or_24 (or_24_out, rst, and_24_out);
  and and_24 (and_24_out, decoder_2_out2, decoder_1_out7);
  Multiplexer #(.select(3), .width(32)) multiplexer_6 (
    .in0(R2), .in1(R6), .in2(R10), .in3(R14), .in4(R18), .in5(R22), .in6(R26), .in7(R30),
    .out(multiplexer_6_out), .sel(Aread0[4:2]));
  Multiplexer #(.select(3), .width(32)) multiplexer_7 (
    .in0(R2), .in1(R6), .in2(R10), .in3(R14), .in4(R18), .in5(R22), .in6(R26), .in7(R30),
    .out(multiplexer_7_out), .sel(Aread1[4:2]));
  Register #(.width(32)) register_25 (.D(multiplexer_1_out), .en(or_25_out), .clk(clk), .Q(R3));  // open: clr
  or or_25 (or_25_out, rst, and_25_out);
  and and_25 (and_25_out, decoder_2_out3, decoder_1_out0);
  Register #(.width(32)) register_26 (.D(multiplexer_1_out), .en(or_26_out), .clk(clk), .Q(R7));  // open: clr
  or or_26 (or_26_out, rst, and_26_out);
  and and_26 (and_26_out, decoder_2_out3, decoder_1_out1);
  Register #(.width(32)) register_27 (.D(multiplexer_1_out), .en(or_27_out), .clk(clk), .Q(R11));  // open: clr
  or or_27 (or_27_out, rst, and_27_out);
  and and_27 (and_27_out, decoder_2_out3, decoder_1_out2);
  Register #(.width(32)) register_28 (.D(multiplexer_1_out), .en(or_28_out), .clk(clk), .Q(R15));  // open: clr
  or or_28 (or_28_out, rst, and_28_out);
  and and_28 (and_28_out, decoder_2_out3, decoder_1_out3);
  Register #(.width(32)) register_29 (.D(multiplexer_1_out), .en(or_29_out), .clk(clk), .Q(R19));  // open: clr
  or or_29 (or_29_out, rst, and_29_out);
  and and_29 (and_29_out, decoder_2_out3, decoder_1_out4);
  Register #(.width(32)) register_30 (.D(multiplexer_1_out), .en(or_30_out), .clk(clk), .Q(R23));  // open: clr
  or or_30 (or_30_out, rst, and_30_out);
  and and_30 (and_30_out, decoder_2_out3, decoder_1_out5);
  Register #(.width(32)) register_31 (.D(multiplexer_1_out), .en(or_31_out), .clk(clk), .Q(R27));  // open: clr
  or or_31 (or_31_out, rst, and_31_out);
  and and_31 (and_31_out, decoder_2_out3, decoder_1_out6);
  Register #(.width(32)) register_32 (.D(multiplexer_1_out), .en(or_32_out), .clk(clk), .Q(R31));  // open: clr
  or or_32 (or_32_out, rst, and_32_out);
  and and_32 (and_32_out, decoder_2_out3, decoder_1_out7);
  Multiplexer #(.select(3), .width(32)) multiplexer_8 (
    .in0(R3), .in1(R7), .in2(R11), .in3(R15), .in4(R19), .in5(R23), .in6(R27), .in7(R31),
    .out(multiplexer_8_out), .sel(Aread0[4:2]));
  Multiplexer #(.select(3), .width(32)) multiplexer_9 (
    .in0(R3), .in1(R7), .in2(R11), .in3(R15), .in4(R19), .in5(R23), .in6(R27), .in7(R31),
    .out(multiplexer_9_out), .sel(Aread1[4:2]));
  Multiplexer #(.select(2), .width(32)) multiplexer_10 (
    .in0(multiplexer_2_out), .in1(multiplexer_4_out), .in2(multiplexer_6_out), .in3(multiplexer_8_out),
    .out(Dread0), .sel(Aread0[1:0]));
  Multiplexer #(.select(2), .width(32)) multiplexer_11 (
    .in0(multiplexer_3_out), .in1(multiplexer_5_out), .in2(multiplexer_7_out), .in3(multiplexer_9_out),
    .out(Dread1), .sel(Aread1[1:0]));

  // Notes on the sheet:
  //   Field Template
endmodule

module Instruction_Decoder (
  input  [31:0] instruction,
  output [15:0] immediate,
  output [5:0] funct,
  output [4:0] shift,
  output [4:0] rd,
  output [4:0] rt,
  output [4:0] rs,
  output [5:0] opcode
);


  assign funct = instruction[5:0];
  assign immediate = instruction[15:0];
  assign opcode = instruction[31:26];
  assign rd = instruction[15:11];
  assign rs = instruction[25:21];
  assign rt = instruction[20:16];
  assign shift = instruction[10:6];
endmodule

module clz (
  input  [31:0] in1,
  output [5:0] out1
);

  wire multiplexer_5_out, not_1_out, not_2_out;
  wire [1:0] multiplexer_4_out;
  wire [3:0] multiplexer_3_out;
  wire [4:0] nor_1_out;
  wire [5:0] bit_extender_1_out;
  wire [7:0] multiplexer_2_out;
  wire [15:0] multiplexer_1_out;

  Comparator #(.mode("unsigned"), .width(16)) comparator_1 (
    .a(in1[31:16]), .b({16{1'b0}}), .eq(nor_1_out[4]));  // open: gt, lt
  Multiplexer #(.width(16)) multiplexer_1 (
    .in0(in1[31:16]), .in1(in1[15:0]), .out(multiplexer_1_out), .sel(nor_1_out[4]));
  Comparator #(.mode("unsigned")) comparator_2 (
    .a(multiplexer_1_out[15:8]), .b({8{1'b0}}), .eq(nor_1_out[3]));  // open: gt, lt
  Multiplexer #(.width(8)) multiplexer_2 (
    .in0(multiplexer_1_out[15:8]), .in1(multiplexer_1_out[7:0]), .out(multiplexer_2_out), .sel(nor_1_out[3]));
  Comparator #(.mode("unsigned"), .width(4)) comparator_3 (
    .a(multiplexer_2_out[7:4]), .b(4'b0000), .eq(nor_1_out[2]));  // open: gt, lt
  Multiplexer #(.width(4)) multiplexer_3 (
    .in0(multiplexer_2_out[7:4]), .in1(multiplexer_2_out[3:0]), .out(multiplexer_3_out), .sel(nor_1_out[2]));
  Comparator #(.mode("unsigned"), .width(2)) comparator_4 (
    .a(multiplexer_3_out[3:2]), .b(2'b00), .eq(nor_1_out[1]));  // open: gt, lt
  nor nor_1 (nor_1_out[0], 1'b0, multiplexer_4_out[1]);
  Multiplexer #(.width(2)) multiplexer_4 (
    .in0(multiplexer_3_out[3:2]), .in1(multiplexer_3_out[1:0]), .out(multiplexer_4_out), .sel(nor_1_out[1]));
  not not_1 (not_1_out, multiplexer_4_out[1]);
  not not_2 (not_2_out, multiplexer_4_out[0]);
  Multiplexer multiplexer_5 (.in0(not_1_out), .in1(not_2_out), .out(multiplexer_5_out), .sel(nor_1_out[0]));
  Adder #(.width(6)) adder_1 (.a({1'b0, nor_1_out}), .b(bit_extender_1_out), .out(out1));  // open: cin, cout
  assign bit_extender_1_out = {{5{1'b0}}, multiplexer_5_out};  // Bit_Extender bit_extender_1
endmodule

module clo (
  input  [31:0] in1,
  output [5:0] out1
);

  wire multiplexer_5_out;
  wire [1:0] multiplexer_4_out;
  wire [3:0] multiplexer_3_out;
  wire [4:0] and_1_out;
  wire [5:0] bit_extender_1_out;
  wire [7:0] multiplexer_2_out;
  wire [15:0] multiplexer_1_out;

  Comparator #(.mode("unsigned"), .width(16)) comparator_1 (
    .a(in1[31:16]), .b({16{1'b1}}), .eq(and_1_out[4]));  // open: gt, lt
  Multiplexer #(.width(16)) multiplexer_1 (
    .in0(in1[31:16]), .in1(in1[15:0]), .out(multiplexer_1_out), .sel(and_1_out[4]));
  Comparator #(.mode("unsigned")) comparator_2 (
    .a(multiplexer_1_out[15:8]), .b({8{1'b1}}), .eq(and_1_out[3]));  // open: gt, lt
  Multiplexer #(.width(8)) multiplexer_2 (
    .in0(multiplexer_1_out[15:8]), .in1(multiplexer_1_out[7:0]), .out(multiplexer_2_out), .sel(and_1_out[3]));
  Comparator #(.mode("unsigned"), .width(4)) comparator_3 (
    .a(multiplexer_2_out[7:4]), .b(4'b1111), .eq(and_1_out[2]));  // open: gt, lt
  Multiplexer #(.width(4)) multiplexer_3 (
    .in0(multiplexer_2_out[7:4]), .in1(multiplexer_2_out[3:0]), .out(multiplexer_3_out), .sel(and_1_out[2]));
  Comparator #(.mode("unsigned"), .width(2)) comparator_4 (
    .a(multiplexer_3_out[3:2]), .b(2'b11), .eq(and_1_out[1]));  // open: gt, lt
  and and_1 (and_1_out[0], 1'b1, multiplexer_4_out[1]);
  Multiplexer #(.width(2)) multiplexer_4 (
    .in0(multiplexer_3_out[3:2]), .in1(multiplexer_3_out[1:0]), .out(multiplexer_4_out), .sel(and_1_out[1]));
  Multiplexer multiplexer_5 (
    .in0(multiplexer_4_out[1]), .in1(multiplexer_4_out[0]), .out(multiplexer_5_out), .sel(and_1_out[0]));
  Adder #(.width(6)) adder_1 (.a({1'b0, and_1_out}), .b(bit_extender_1_out), .out(out1));  // open: cin, cout
  assign bit_extender_1_out = {{5{1'b0}}, multiplexer_5_out};  // Bit_Extender bit_extender_1
endmodule

module add_sub (
  input  c_in,
  input  sub_notAdd,
  input  [31:0] in1,
  input  [31:0] in2,
  output [31:0] s,
  output c
);

  wire adder_1_cout, adder_2_cout, adder_3_cout, adder_4_cout, adder_5_cout, adder_6_cout, adder_7_cout,
       adder_8_cout, adder_9_cout, adder_10_cout, adder_11_cout, adder_12_cout, adder_13_cout, adder_14_cout,
       adder_15_cout, multiplexer_2_out, multiplexer_4_out, multiplexer_6_out, multiplexer_8_out,
       multiplexer_10_out, multiplexer_14_out;
  wire [3:0] adder_1_out, adder_2_out, adder_3_out, adder_4_out, adder_5_out, adder_6_out, adder_7_out,
       adder_8_out, adder_9_out, adder_10_out, adder_11_out, adder_12_out, adder_13_out, adder_14_out;
  wire [31:0] bit_extender_1_out, xor_1_out;

  assign xor_1_out = in2 ^ bit_extender_1_out;  // XOR_Gate xor_1, 32 bits wide
  Adder #(.width(4)) adder_1 (.a(xor_1_out[11:8]), .b(in1[11:8]), .out(adder_1_out), .cin(1'b0), .cout(adder_1_cout));
  Adder #(.width(4)) adder_2 (.a(xor_1_out[15:12]), .b(in1[15:12]), .out(adder_2_out), .cin(1'b0), .cout(adder_2_cout));
  Adder #(.width(4)) adder_3 (.a(xor_1_out[19:16]), .b(in1[19:16]), .out(adder_3_out), .cin(1'b0), .cout(adder_3_cout));
  Adder #(.width(4)) adder_4 (.a(xor_1_out[23:20]), .b(in1[23:20]), .out(adder_4_out), .cin(1'b0), .cout(adder_4_cout));
  Adder #(.width(4)) adder_5 (.a(xor_1_out[27:24]), .b(in1[27:24]), .out(adder_5_out), .cin(1'b0), .cout(adder_5_cout));
  Adder #(.width(4)) adder_6 (.a(xor_1_out[31:28]), .b(in1[31:28]), .out(adder_6_out), .cin(1'b0), .cout(adder_6_cout));
  assign bit_extender_1_out = {{31{sub_notAdd}}, sub_notAdd};  // Bit_Extender bit_extender_1
  Adder #(.width(4)) adder_7 (.a(xor_1_out[7:4]), .b(in1[7:4]), .out(adder_7_out), .cin(1'b0), .cout(adder_7_cout));
  Adder #(.width(4)) adder_8 (.a(xor_1_out[7:4]), .b(in1[7:4]), .out(adder_8_out), .cin(1'b1), .cout(adder_8_cout));
  Adder #(.width(4)) adder_9 (.a(xor_1_out[11:8]), .b(in1[11:8]), .out(adder_9_out), .cin(1'b1), .cout(adder_9_cout));
  Adder #(.width(4)) adder_10 (
    .a(xor_1_out[15:12]), .b(in1[15:12]), .out(adder_10_out), .cin(1'b1), .cout(adder_10_cout));
  Adder #(.width(4)) adder_11 (
    .a(xor_1_out[19:16]), .b(in1[19:16]), .out(adder_11_out), .cin(1'b1), .cout(adder_11_cout));
  Adder #(.width(4)) adder_12 (
    .a(xor_1_out[23:20]), .b(in1[23:20]), .out(adder_12_out), .cin(1'b1), .cout(adder_12_cout));
  Adder #(.width(4)) adder_13 (
    .a(xor_1_out[27:24]), .b(in1[27:24]), .out(adder_13_out), .cin(1'b1), .cout(adder_13_cout));
  Adder #(.width(4)) adder_14 (
    .a(xor_1_out[31:28]), .b(in1[31:28]), .out(adder_14_out), .cin(1'b1), .cout(adder_14_cout));
  Adder #(.width(4)) adder_15 (.a(xor_1_out[3:0]), .b(in1[3:0]), .out(s[3:0]), .cin(c_in), .cout(adder_15_cout));
  Multiplexer #(.width(4)) multiplexer_1 (
    .in0(adder_1_out), .in1(adder_9_out), .out(s[11:8]), .sel(multiplexer_14_out));
  Multiplexer multiplexer_2 (.in0(adder_1_cout), .in1(adder_9_cout), .out(multiplexer_2_out), .sel(multiplexer_14_out));
  Multiplexer #(.width(4)) multiplexer_3 (
    .in0(adder_2_out), .in1(adder_10_out), .out(s[15:12]), .sel(multiplexer_2_out));
  Multiplexer multiplexer_4 (.in0(adder_2_cout), .in1(adder_10_cout), .out(multiplexer_4_out), .sel(multiplexer_2_out));
  Multiplexer #(.width(4)) multiplexer_5 (
    .in0(adder_3_out), .in1(adder_11_out), .out(s[19:16]), .sel(multiplexer_4_out));
  Multiplexer multiplexer_6 (.in0(adder_3_cout), .in1(adder_11_cout), .out(multiplexer_6_out), .sel(multiplexer_4_out));
  Multiplexer #(.width(4)) multiplexer_7 (
    .in0(adder_4_out), .in1(adder_12_out), .out(s[23:20]), .sel(multiplexer_6_out));
  Multiplexer multiplexer_8 (.in0(adder_4_cout), .in1(adder_12_cout), .out(multiplexer_8_out), .sel(multiplexer_6_out));
  Multiplexer #(.width(4)) multiplexer_9 (
    .in0(adder_5_out), .in1(adder_13_out), .out(s[27:24]), .sel(multiplexer_8_out));
  Multiplexer multiplexer_10 (
    .in0(adder_5_cout), .in1(adder_13_cout), .out(multiplexer_10_out), .sel(multiplexer_8_out));
  Multiplexer #(.width(4)) multiplexer_11 (
    .in0(adder_6_out), .in1(adder_14_out), .out(s[31:28]), .sel(multiplexer_10_out));
  Multiplexer multiplexer_12 (.in0(adder_6_cout), .in1(adder_14_cout), .out(c), .sel(multiplexer_10_out));
  Multiplexer #(.width(4)) multiplexer_13 (.in0(adder_7_out), .in1(adder_8_out), .out(s[7:4]), .sel(adder_15_cout));
  Multiplexer multiplexer_14 (.in0(adder_7_cout), .in1(adder_8_cout), .out(multiplexer_14_out), .sel(adder_15_cout));
endmodule

module mul (
  input  [31:0] multiplicand,
  input  [31:0] mutiplier,
  input  clk,
  input  strat,
  output done,
  output [63:0] result
);

  wire A0_c, A1_c;
  wire [1:0] A3_carry, register_2_q, register_2_q_2, register_2_q_3, register_2_q_4, register_2_q_5,
       register_2_q_6, register_2_q_7, register_2_q_8, register_2_q_9, register_2_q_10, register_2_q_11,
       register_2_q_12, register_2_q_13, register_2_q_14, register_2_q_15, register_2_q_16;
  wire [31:0] A0_s, A1_s, A2_s, A3_sum, A4_sum, A5_s, A7_s, bit_extender_2_out, carry_q, multiplexer_2_out,
       multiplexer_4_out, multiplexer_6_out, register_1_q, register_1_q_2, shifter_1_out, shifter_1_out_2,
       shifter_2_out, shifter_3_out, temp_res_q;
  wire [63:0] bit_extender_1_out, multiplexer_1_out, multiplexer_3_out, multiplexer_5_out, shifter_4_out,
       shifter_5_out;

  assign bit_extender_1_out = {{32{1'b0}}, multiplicand};  // Bit_Extender bit_extender_1
  Counter #(.max('he), .width(4)) counter_1 (
    .clr(strat), .load(strat), .clk(clk), .carry(done));  // open: up, count, D, Q
  Multiplexer #(.width(64)) multiplexer_1 (
    .in0(shifter_5_out), .in1(bit_extender_1_out), .out(multiplexer_1_out), .sel(strat));
  Multiplexer #(.width(32)) multiplexer_2 (.in0(shifter_3_out), .in1(mutiplier), .out(multiplexer_2_out), .sel(strat));
  Register #(.width(64)) register_1 (
    .D(multiplexer_1_out), .en(1'b1), .clk(clk), .Q({register_1_q_2, register_1_q}));  // open: clr
  Register #(.width(32)) register_2 (
    .D(multiplexer_2_out), .en(1'b1), .clk(clk),
    .Q({register_2_q_16, register_2_q_15, register_2_q_14, register_2_q_13, register_2_q_12, register_2_q_11, register_2_q_10, register_2_q_9, register_2_q_8, register_2_q_7, register_2_q_6, register_2_q_5, register_2_q_4, register_2_q_3, register_2_q_2, register_2_q}));  // open: clr
  Shifter #(.width(64)) shifter_1 (
    .in({register_1_q_2, register_1_q}), .\dist (6'b000001), .out({shifter_1_out_2, shifter_1_out}));
  Shifter #(.shift("lr"), .width(32)) shifter_2 (
    .in({register_2_q_16, register_2_q_15, register_2_q_14, register_2_q_13, register_2_q_12, register_2_q_11, register_2_q_10, register_2_q_9, register_2_q_8, register_2_q_7, register_2_q_6, register_2_q_5, register_2_q_4, register_2_q_3, register_2_q_2, register_2_q}),
    .\dist (5'b00001), .out(shifter_2_out));
  Shifter #(.shift("lr"), .width(32)) shifter_3 (.in(shifter_2_out), .\dist (5'b00001), .out(shifter_3_out));
  Shifter #(.width(64)) shifter_4 (.in({register_1_q_2, register_1_q}), .\dist (6'b000001), .out(shifter_4_out));
  Shifter #(.width(64)) shifter_5 (.in(shifter_4_out), .\dist (6'b000001), .out(shifter_5_out));
  carrySaveAdder A3 (.in1(register_1_q), .in2(shifter_1_out), .in3(result[31:0]), .sum(A3_sum), .carry(A3_carry));
  carrySaveAdder A4 (.in1(register_1_q_2), .in2(shifter_1_out_2), .in3(temp_res_q), .sum(A4_sum));  // open: carry
  carrySelectAdder A0 (.c_in(1'b0), .in1(register_1_q), .in2(result[31:0]), .s(A0_s), .c(A0_c));
  carrySelectAdder A7 (.c_in(A0_c), .in1(register_1_q_2), .in2(temp_res_q), .s(A7_s));  // open: c
  carrySelectAdder A1 (.c_in(1'b0), .in1(shifter_1_out), .in2(result[31:0]), .s(A1_s), .c(A1_c));
  carrySelectAdder A2 (.c_in(A1_c), .in1(shifter_1_out_2), .in2(temp_res_q), .s(A2_s));  // open: c
  assign bit_extender_2_out = {{30{1'b0}}, A3_carry};  // Bit_Extender bit_extender_2
  Multiplexer #(.select(2), .width(64)) multiplexer_3 (
    .in0({temp_res_q, result[31:0]}), .in1({A7_s, A0_s}), .in2({A2_s, A1_s}), .in3({A4_sum, A3_sum}),
    .out(multiplexer_3_out), .sel(register_2_q));
  carrySelectAdder A5 (.c_in(1'b0), .in1(bit_extender_2_out), .in2(carry_q), .s(A5_s));  // open: c
  Multiplexer #(.select(2), .width(32)) multiplexer_4 (
    .in0(carry_q), .in1(carry_q), .in2(carry_q), .in3(A5_s), .out(multiplexer_4_out), .sel(register_2_q));
  Multiplexer #(.width(64)) multiplexer_5 (
    .in0(multiplexer_3_out), .in1({64{1'b0}}), .out(multiplexer_5_out), .sel(strat));
  Multiplexer #(.width(32)) multiplexer_6 (
    .in0(multiplexer_4_out), .in1({32{1'b0}}), .out(multiplexer_6_out), .sel(strat));
  Register #(.width(64)) temp_res (
    .D(multiplexer_5_out), .en(1'b1), .clk(clk), .Q({temp_res_q, result[31:0]}));  // open: clr
  Register #(.width(32)) carry (.D(multiplexer_6_out), .en(1'b1), .clk(clk), .Q(carry_q));  // open: clr
  carrySelectAdder A6 (.c_in(1'b0), .in1(temp_res_q), .in2(carry_q), .s(result[63:32]));  // open: c
endmodule

module carrySelectAdder (
  input  c_in,
  input  [31:0] in1,
  input  [31:0] in2,
  output [31:0] s,
  output c
);

  wire adder_1_cout, adder_2_cout, adder_3_cout, adder_4_cout, adder_5_cout, adder_6_cout, adder_7_cout,
       adder_8_cout, adder_9_cout, adder_10_cout, adder_11_cout, adder_12_cout, adder_13_cout, adder_14_cout,
       adder_15_cout, multiplexer_2_out, multiplexer_4_out, multiplexer_6_out, multiplexer_8_out,
       multiplexer_10_out, multiplexer_14_out;
  wire [3:0] adder_1_out, adder_2_out, adder_3_out, adder_4_out, adder_5_out, adder_6_out, adder_7_out,
       adder_8_out, adder_9_out, adder_10_out, adder_11_out, adder_12_out, adder_13_out, adder_14_out;

  Adder #(.width(4)) adder_1 (.a(in2[11:8]), .b(in1[11:8]), .out(adder_1_out), .cin(1'b0), .cout(adder_1_cout));
  Adder #(.width(4)) adder_2 (.a(in2[15:12]), .b(in1[15:12]), .out(adder_2_out), .cin(1'b0), .cout(adder_2_cout));
  Adder #(.width(4)) adder_3 (.a(in2[19:16]), .b(in1[19:16]), .out(adder_3_out), .cin(1'b0), .cout(adder_3_cout));
  Adder #(.width(4)) adder_4 (.a(in2[23:20]), .b(in1[23:20]), .out(adder_4_out), .cin(1'b0), .cout(adder_4_cout));
  Adder #(.width(4)) adder_5 (.a(in2[27:24]), .b(in1[27:24]), .out(adder_5_out), .cin(1'b0), .cout(adder_5_cout));
  Adder #(.width(4)) adder_6 (.a(in2[31:28]), .b(in1[31:28]), .out(adder_6_out), .cin(1'b0), .cout(adder_6_cout));
  Adder #(.width(4)) adder_7 (.a(in2[7:4]), .b(in1[7:4]), .out(adder_7_out), .cin(1'b0), .cout(adder_7_cout));
  Adder #(.width(4)) adder_8 (.a(in2[7:4]), .b(in1[7:4]), .out(adder_8_out), .cin(1'b1), .cout(adder_8_cout));
  Adder #(.width(4)) adder_9 (.a(in2[11:8]), .b(in1[11:8]), .out(adder_9_out), .cin(1'b1), .cout(adder_9_cout));
  Adder #(.width(4)) adder_10 (.a(in2[15:12]), .b(in1[15:12]), .out(adder_10_out), .cin(1'b1), .cout(adder_10_cout));
  Adder #(.width(4)) adder_11 (.a(in2[19:16]), .b(in1[19:16]), .out(adder_11_out), .cin(1'b1), .cout(adder_11_cout));
  Adder #(.width(4)) adder_12 (.a(in2[23:20]), .b(in1[23:20]), .out(adder_12_out), .cin(1'b1), .cout(adder_12_cout));
  Adder #(.width(4)) adder_13 (.a(in2[27:24]), .b(in1[27:24]), .out(adder_13_out), .cin(1'b1), .cout(adder_13_cout));
  Adder #(.width(4)) adder_14 (.a(in2[31:28]), .b(in1[31:28]), .out(adder_14_out), .cin(1'b1), .cout(adder_14_cout));
  Adder #(.width(4)) adder_15 (.a(in2[3:0]), .b(in1[3:0]), .out(s[3:0]), .cin(c_in), .cout(adder_15_cout));
  Multiplexer #(.width(4)) multiplexer_1 (
    .in0(adder_1_out), .in1(adder_9_out), .out(s[11:8]), .sel(multiplexer_14_out));
  Multiplexer multiplexer_2 (.in0(adder_1_cout), .in1(adder_9_cout), .out(multiplexer_2_out), .sel(multiplexer_14_out));
  Multiplexer #(.width(4)) multiplexer_3 (
    .in0(adder_2_out), .in1(adder_10_out), .out(s[15:12]), .sel(multiplexer_2_out));
  Multiplexer multiplexer_4 (.in0(adder_2_cout), .in1(adder_10_cout), .out(multiplexer_4_out), .sel(multiplexer_2_out));
  Multiplexer #(.width(4)) multiplexer_5 (
    .in0(adder_3_out), .in1(adder_11_out), .out(s[19:16]), .sel(multiplexer_4_out));
  Multiplexer multiplexer_6 (.in0(adder_3_cout), .in1(adder_11_cout), .out(multiplexer_6_out), .sel(multiplexer_4_out));
  Multiplexer #(.width(4)) multiplexer_7 (
    .in0(adder_4_out), .in1(adder_12_out), .out(s[23:20]), .sel(multiplexer_6_out));
  Multiplexer multiplexer_8 (.in0(adder_4_cout), .in1(adder_12_cout), .out(multiplexer_8_out), .sel(multiplexer_6_out));
  Multiplexer #(.width(4)) multiplexer_9 (
    .in0(adder_5_out), .in1(adder_13_out), .out(s[27:24]), .sel(multiplexer_8_out));
  Multiplexer multiplexer_10 (
    .in0(adder_5_cout), .in1(adder_13_cout), .out(multiplexer_10_out), .sel(multiplexer_8_out));
  Multiplexer #(.width(4)) multiplexer_11 (
    .in0(adder_6_out), .in1(adder_14_out), .out(s[31:28]), .sel(multiplexer_10_out));
  Multiplexer multiplexer_12 (.in0(adder_6_cout), .in1(adder_14_cout), .out(c), .sel(multiplexer_10_out));
  Multiplexer #(.width(4)) multiplexer_13 (.in0(adder_7_out), .in1(adder_8_out), .out(s[7:4]), .sel(adder_15_cout));
  Multiplexer multiplexer_14 (.in0(adder_7_cout), .in1(adder_8_cout), .out(multiplexer_14_out), .sel(adder_15_cout));
endmodule

module carrySaveAdder (
  input  [31:0] in1,
  input  [31:0] in2,
  input  [31:0] in3,
  output [31:0] sum,
  output [1:0] carry
);

  wire A_c;
  wire [31:0] and_1_out, and_2_out, and_3_out, or_1_out, xor_1_out, xor_2_out;

  assign xor_1_out = in1 ^ in2;  // XOR_Gate xor_1, 32 bits wide
  assign and_1_out = in1 & in2;  // AND_Gate and_1, 32 bits wide
  assign and_2_out = in2 & in3;  // AND_Gate and_2, 32 bits wide
  assign and_3_out = in1 & in3;  // AND_Gate and_3, 32 bits wide
  assign xor_2_out = xor_1_out ^ in3;  // XOR_Gate xor_2, 32 bits wide
  assign or_1_out = and_1_out | and_2_out | and_3_out;  // OR_Gate or_1, 32 bits wide
  carrySelectAdder A (.c_in(1'b0), .in1(xor_2_out), .in2({or_1_out[30:0], 1'b0}), .s(sum), .c(A_c));
  xor xor_3 (carry[0], A_c, or_1_out[31]);
  and and_4 (carry[1], A_c, or_1_out[31]);
endmodule

module div (
  input  clk,
  input  start,
  input  [31:0] dividend,
  input  [31:0] divisor,
  output [31:0] remainder,
  output [31:0] quotient,
  output done
);

  wire comparator_1_eq, not_1_out, not_2_out;
  wire [0:0] comparator_2_lt;
  wire [31:0] b_q, multiplexer_1_out, multiplexer_2_out, multiplexer_3_out, multiplexer_4_out,
       multiplexer_5_out, register_1_q, subtractor_1_out, subtractor_2_out;
  wire [63:0] shifter_1_out;

  Multiplexer #(.select(2), .width(32)) multiplexer_1 (
    .in0(shifter_1_out[31:0]), .in1(shifter_1_out[31:0]), .in2({quotient[31:1], 1'b1}), .in3(quotient),
    .out(multiplexer_1_out), .sel({register_1_q[0], comparator_2_lt[0]}));
  Multiplexer #(.select(2), .width(32)) multiplexer_2 (
    .in0(shifter_1_out[63:32]), .in1(shifter_1_out[63:32]), .in2(subtractor_2_out), .in3(remainder),
    .out(multiplexer_2_out), .sel({register_1_q[0], comparator_2_lt[0]}));
  Multiplexer #(.width(32)) multiplexer_3 (.in0(subtractor_1_out), .in1(32'h40), .out(multiplexer_3_out), .sel(start));
  Multiplexer #(.width(32)) multiplexer_4 (
    .in0(multiplexer_2_out), .in1({32{1'b0}}), .out(multiplexer_4_out), .sel(start));
  Multiplexer #(.width(32)) multiplexer_5 (
    .in0(multiplexer_1_out), .in1(dividend), .out(multiplexer_5_out), .sel(start));
  Register #(.width(32)) a (.D(multiplexer_4_out), .en(not_1_out), .clk(clk), .Q(remainder));  // open: clr
  Register #(.width(32)) b (.D(divisor), .en(start), .clk(clk), .Q(b_q));  // open: clr
  Register #(.width(32)) q (.D(multiplexer_5_out), .en(not_1_out), .clk(clk), .Q(quotient));  // open: clr
  Register #(.width(32)) register_1 (.D(multiplexer_3_out), .en(not_1_out), .clk(clk), .Q(register_1_q));  // open: clr
  Subtractor #(.width(32)) subtractor_1 (.a(register_1_q), .b(32'h1), .out(subtractor_1_out));  // open: bin, bout
  Shifter #(.width(64)) shifter_1 (.in({remainder, quotient}), .\dist (6'b000001), .out(shifter_1_out));
  Comparator #(.width(32)) comparator_1 (.a(register_1_q), .b({32{1'b0}}), .eq(comparator_1_eq));  // open: gt, lt
  not not_1 (not_1_out, done);
  Comparator #(.mode("unsigned"), .width(32)) comparator_2 (
    .a(remainder), .b(b_q), .lt(comparator_2_lt[0]));  // open: gt, eq
  not not_2 (not_2_out, start);
  Subtractor #(.width(32)) subtractor_2 (.a(remainder), .b(b_q), .out(subtractor_2_out));  // open: bin, bout
  and and_1 (done, comparator_1_eq, not_2_out);
endmodule

module srlShift (
  input  [31:0] in1,
  input  [4:0] shift,
  output [31:0] out1
);

  Multiplexer #(.select(5), .width(32)) multiplexer_1 (
    .in0(in1), .in1({1'b0, in1[31:1]}), .in2({2'b00, in1[31:2]}), .in3({3'b000, in1[31:3]}),
    .in4({4'b0000, in1[31:4]}), .in5({{5{1'b0}}, in1[31:5]}), .in6({{6{1'b0}}, in1[31:6]}),
    .in7({{7{1'b0}}, in1[31:7]}), .in8({{8{1'b0}}, in1[31:8]}), .in9({{9{1'b0}}, in1[31:9]}),
    .in10({{10{1'b0}}, in1[31:10]}), .in11({{11{1'b0}}, in1[31:11]}), .in12({{12{1'b0}}, in1[31:12]}),
    .in13({{13{1'b0}}, in1[31:13]}), .in14({{14{1'b0}}, in1[31:14]}), .in15({{15{1'b0}}, in1[31:15]}),
    .in16({{16{1'b0}}, in1[31:16]}), .in17({{17{1'b0}}, in1[31:17]}), .in18({{18{1'b0}}, in1[31:18]}),
    .in19({{19{1'b0}}, in1[31:19]}), .in20({{20{1'b0}}, in1[31:20]}), .in21({{21{1'b0}}, in1[31:21]}),
    .in22({{22{1'b0}}, in1[31:22]}), .in23({{23{1'b0}}, in1[31:23]}), .in24({{24{1'b0}}, in1[31:24]}),
    .in25({{25{1'b0}}, in1[31:25]}), .in26({{26{1'b0}}, in1[31:26]}), .in27({{27{1'b0}}, in1[31:27]}),
    .in28({{28{1'b0}}, in1[31:28]}), .in29({{29{1'b0}}, in1[31:29]}), .in30({{30{1'b0}}, in1[31:30]}),
    .in31({{31{1'b0}}, in1[31]}), .out(out1), .sel(shift));
endmodule

module ALU (
  input  [31:0] a,
  input  [31:0] b,
  input  rst,
  input  [3:0] aluop,
  input  output_inc,
  input  output_inverted,
  input  clk,
  output [31:0] res_low,
  output [31:0] res_high,
  output done
);

  wire add_c, comparator_1_eq, comparator_2_eq, comparator_4_lt, comparator_5_eq, comparator_6_eq, div_done,
       mul_done, multiplexer_3_out, or_2_out, or_3_out, or_4_out, or_5_out, or_6_out, or_7_out, or_8_out,
       start;
  wire [3:0] register_1_q, xor_2_out;
  wire [4:0] not_b, subtractor_2_out;
  wire [5:0] b_1, bit_extender_5_out, bit_extender_6_out, clo_circ_out1, clz_circ_out1, shifter_1_out;
  wire [31:0] add_s, and_1_out, bit_extender_1_out, bit_extender_2_out, bit_extender_3_out, high_div,
       high_sll, high_sra, low_div, low_rotr, low_sll, low_sra, low_srl, or_1_out, q, register_2_q,
       register_3_q, remainder, sub_s, subtractor_1_out, xor_1_out, xor_3_out, xor_4_out;
  wire [31:31] high_sub;
  wire [63:0] mul_circ_result, multiplexer_5_out, multiplexer_9_out, multiplexer_11_out, not_1_out, result,
       shifter_3_out, shifter_4_out, shifter_5_out, shifter_6_out, shifter_7_out, shifter_8_out;

  assign and_1_out = a & b;  // AND_Gate and_1, 32 bits wide
  assign or_1_out = a | b;  // OR_Gate or_1, 32 bits wide
  assign xor_1_out = a ^ b;  // XOR_Gate xor_1, 32 bits wide
  add_sub add (.c_in(aluop[0]), .sub_notAdd(aluop[0]), .in1(a), .in2(b), .s(add_s), .c(add_c));
  add_sub sub (.c_in(aluop[0]), .sub_notAdd(aluop[0]), .in1(a), .in2(b), .s(sub_s));  // open: c
  mul mul_circ (.multiplicand(a), .mutiplier(b), .clk(clk), .strat(start), .done(mul_done), .result(mul_circ_result));
  div div_circ (
    .clk(clk), .start(start), .dividend(a), .divisor(b), .remainder(remainder), .quotient(q), .done(div_done));
  clz clz_circ (.in1(a), .out1(clz_circ_out1));
  clo clo_circ (.in1(a), .out1(clo_circ_out1));
  assign bit_extender_1_out = {{26{1'b0}}, clo_circ_out1};  // Bit_Extender bit_extender_1
  assign bit_extender_2_out = {{26{1'b0}}, clz_circ_out1};  // Bit_Extender bit_extender_2
  Register #(.width(4)) register_1 (.D(aluop), .en(1'b1), .clk(clk), .Q(register_1_q));  // open: clr
  Comparator #(.width(4)) comparator_1 (.a(aluop), .b(4'b0010), .eq(comparator_1_eq));  // open: gt, lt
  Comparator #(.width(4)) comparator_2 (.a(aluop), .b(4'b0011), .eq(comparator_2_eq));  // open: gt, lt
  or or_2 (or_2_out, comparator_1_eq, comparator_2_eq);
  assign bit_extender_3_out = {{31{1'b0}}, add_c};  // Bit_Extender bit_extender_3
  Register #(.width(32)) register_2 (.D(a), .en(1'b1), .clk(clk), .Q(register_2_q));  // open: clr
  Register #(.width(32)) register_3 (.D(b), .en(1'b1), .clk(clk), .Q(register_3_q));  // open: clr
  assign xor_2_out = register_1_q ^ aluop;  // XOR_Gate xor_2, 4 bits wide
  Multiplexer #(.select(4), .width(32)) multiplexer_1 (
    .in0(add_s), .in1(sub_s), .in2(mul_circ_result[31:0]), .in3(low_div), .in4(and_1_out), .in5(or_1_out),
    .in6(xor_1_out), .in7(bit_extender_1_out), .in8(bit_extender_2_out), .in9(low_sll), .in10(low_srl),
    .in11(low_sra), .in12(low_rotr), .out(result[31:0]), .sel(aluop));  // open: in13, in14, in15
  Multiplexer #(.select(4), .width(32)) multiplexer_2 (
    .in0(bit_extender_3_out), .in1({32{high_sub[31]}}), .in2(mul_circ_result[63:32]), .in3(high_div),
    .in4({32{1'b0}}), .in5({32{1'b0}}), .in6({32{1'b0}}), .in7({32{1'b0}}), .in8({32{1'b0}}), .in9(high_sll),
    .in10({32{1'b0}}), .in11(high_sra), .in12({32{1'b0}}), .out(result[63:32]), .sel(aluop));  // open: in13, in14, in15
  assign xor_3_out = register_2_q ^ a;  // XOR_Gate xor_3, 32 bits wide
  Multiplexer multiplexer_3 (.in0(mul_done), .in1(div_done), .out(multiplexer_3_out), .sel(comparator_2_eq));
  assign xor_4_out = register_3_q ^ b;  // XOR_Gate xor_4, 32 bits wide
  or or_3 (or_3_out, xor_2_out[0], xor_2_out[1], xor_2_out[3], xor_2_out[2]);
  Multiplexer multiplexer_4 (.in0(1'b1), .in1(multiplexer_3_out), .out(done), .sel(or_2_out));
  or or_4 (or_4_out, xor_3_out[0], xor_3_out[1], xor_3_out[2], xor_3_out[3], xor_3_out[4], xor_3_out[5], xor_3_out[6], xor_3_out[7], xor_3_out[8], xor_3_out[9], xor_3_out[10], xor_3_out[11], xor_3_out[12], xor_3_out[13], xor_3_out[14], xor_3_out[15], xor_3_out[17], xor_3_out[18], xor_3_out[19], xor_3_out[20], xor_3_out[21], xor_3_out[22], xor_3_out[23], xor_3_out[24], xor_3_out[25], xor_3_out[26], xor_3_out[27], xor_3_out[28], xor_3_out[29], xor_3_out[30], xor_3_out[31], xor_3_out[16]);
  or or_5 (or_5_out, xor_4_out[0], xor_4_out[1], xor_4_out[2], xor_4_out[3], xor_4_out[4], xor_4_out[5], xor_4_out[6], xor_4_out[7], xor_4_out[8], xor_4_out[9], xor_4_out[10], xor_4_out[11], xor_4_out[12], xor_4_out[13], xor_4_out[14], xor_4_out[15], xor_4_out[17], xor_4_out[18], xor_4_out[19], xor_4_out[20], xor_4_out[21], xor_4_out[22], xor_4_out[23], xor_4_out[24], xor_4_out[25], xor_4_out[26], xor_4_out[27], xor_4_out[28], xor_4_out[29], xor_4_out[30], xor_4_out[31], xor_4_out[16]);
  Comparator #(.mode("unsigned"), .width(32)) comparator_3 (.a(a), .b(b), .lt(high_sub[31]));  // open: gt, eq
  Subtractor #(.width(32)) subtractor_1 (.a(b), .b(32'h1), .out(subtractor_1_out));  // open: bin, bout
  assign not_1_out = ~result;  // NOT_Gate not_1, 64 bits wide
  or or_6 (or_6_out, or_4_out, or_5_out, or_3_out);
  Shifter #(.width(6)) shifter_1 (.in(subtractor_1_out[5:0]), .\dist (3'b001), .out(shifter_1_out));
  Multiplexer #(.width(64)) multiplexer_5 (
    .in0(result), .in1(not_1_out), .out(multiplexer_5_out), .sel(output_inverted));
  Subtractor #(.width(5)) subtractor_2 (.a({5{1'b1}}), .b(b[4:0]), .out(subtractor_2_out));  // open: bin, bout
  and and_2 (start, or_6_out, or_2_out);
  Shifter #(.shift("lr"), .width(6)) shifter_2 (.in(shifter_1_out), .\dist (3'b001), .out(b_1));
  Adder #(.width(5)) adder_1 (.a(subtractor_2_out), .b(5'b00001), .out(not_b));  // open: cin, cout
  Adder #(.width(64)) adder_2 (
    .a(multiplexer_5_out), .b({{63{1'b0}}, output_inc}), .out({res_high, res_low}));  // open: cin, cout
  assign high_sra = {{31{a[31]}}, a[31]};  // Bit_Extender bit_extender_4
  Comparator #(.mode("unsigned"), .width(32)) comparator_4 (.a(a), .b(b), .lt(comparator_4_lt));  // open: gt, eq
  assign bit_extender_5_out = {{1{1'b0}}, b[4:0]};  // Bit_Extender bit_extender_5
  Multiplexer #(.width(32)) multiplexer_6 (.in0(remainder), .in1(a), .out(high_div), .sel(comparator_4_lt));
  Multiplexer #(.width(32)) multiplexer_7 (.in0(q), .in1({32{1'b0}}), .out(low_div), .sel(comparator_4_lt));
  Shifter #(.width(64)) shifter_3 (.in({{32{1'b0}}, a}), .\dist (bit_extender_5_out), .out(shifter_3_out));
  Shifter #(.shift("ar"), .width(64)) shifter_4 (.in({high_sra, a}), .\dist (b_1), .out(shifter_4_out));
  Shifter #(.shift("lr"), .width(64)) shifter_5 (.in(shifter_3_out), .\dist (6'b000001), .out(shifter_5_out));
  or or_7 (or_7_out, b[0], comparator_5_eq);
  Comparator #(.width(5)) comparator_5 (.a(b[4:0]), .b({5{1'b0}}), .eq(comparator_5_eq));  // open: gt, lt
  Multiplexer #(.width(64)) multiplexer_8 (
    .in0(shifter_5_out), .in1(shifter_3_out), .out({high_sll, low_sll}), .sel(or_7_out));
  Multiplexer #(.width(64)) multiplexer_9 (
    .in0(shifter_6_out), .in1(shifter_4_out), .out(multiplexer_9_out), .sel(b[0]));
  srlShift righeShift (.in1(a), .shift(b[4:0]), .out1(low_srl));
  Shifter #(.shift("ar"), .width(64)) shifter_6 (.in(shifter_4_out), .\dist (6'b000001), .out(shifter_6_out));
  Comparator #(.width(5)) comparator_6 (.a(b[4:0]), .b({5{1'b0}}), .eq(comparator_6_eq));  // open: gt, lt
  assign bit_extender_6_out = {{1{1'b0}}, not_b};  // Bit_Extender bit_extender_6
  Multiplexer #(.width(32)) multiplexer_10 (
    .in0(multiplexer_9_out[31:0]), .in1(a), .out(low_sra), .sel(comparator_6_eq));
  Shifter #(.width(64)) shifter_7 (.in({{32{1'b0}}, a}), .\dist (bit_extender_6_out), .out(shifter_7_out));
  Shifter #(.shift("lr"), .width(64)) shifter_8 (.in(shifter_7_out), .\dist (6'b000001), .out(shifter_8_out));
  or or_8 (or_8_out, not_b[0], comparator_5_eq);
  Multiplexer #(.width(64)) multiplexer_11 (
    .in0(shifter_8_out), .in1(shifter_7_out), .out(multiplexer_11_out), .sel(or_8_out));
  assign low_rotr = low_srl | multiplexer_11_out[31:0];  // OR_Gate or_9, 32 bits wide

  // Other names for the same wires on the sheet: lsb5_b[4:0] = b[4:0]; lsb_b = b[0];
  //   high_sub[30:0] = {31{high_sub[31]}}

  // Notes on the sheet:
  //   a: initial=0x139
endmodule

// 4
module Control_Unit (
  input  zero,
  input  [5:0] opcode,
  input  clk,
  input  rst,
  input  [5:0] func,
  input  syns_in,
  output inst_we,
  output mem_write,
  output pc_we,
  output [2:0] write_addr,
  output [1:0] alu_in2,
  output [1:0] pc_select,
  output [2:0] write_data,
  output alu_in1,
  output [3:0] Aluop,
  output done,
  output we_hilo,
  output syns_out,
  output exchange,
  output [4:0] state
);

  wire and_1_out, and_2_out, and_3_out, and_4_out, and_5_out, and_6_out, and_7_out, and_8_out, and_9_out,
       and_10_out, and_14_out, and_15_out, and_16_out, and_17_out, and_18_out, and_19_out, and_20_out,
       and_22_out, and_23_out, and_26_out, and_28_out, and_29_out, and_30_out, and_31_out, and_32_out,
       and_33_out, and_35_out, and_36_out, and_37_out, and_38_out, and_39_out, and_41_out, and_42_out,
       and_43_out, and_44_out, and_45_out, and_46_out, and_47_out, and_48_out, and_49_out, and_50_out,
       and_51_out, and_52_out, and_53_out, and_54_out, and_55_out, b1, b2, b3, b4, b5, b6, b7, b8, b9, b10,
       b11, b12, b13, b14, b16, b17, b18, b19, b20, b21, b22, b24, b25, b26, d_ff_6_q, div, div_enter,
       dive_done, jr, mfhi, mul_1, mul_enter, n0, n1, n2, n3, n4, n5, nf0, nf1, nf2, nf3, nf4, nf5,
       nor_1_out, not_1_out, not_2_out, not_3_out, not_4_out, not_5_out, not_19_out, ns0, ns1, ns2, ns3, ns4,
       or_3_out, or_6_out, or_9_out, or_13_out, or_22_out, or_23_out, or_24_out, or_25_out, or_26_out,
       or_27_out, or_28_out, or_29_out, or_30_out, or_31_out, or_32_out, or_33_out, or_34_out, R_type, s_in,
       xnor_1_out;
  wire [2:0] or_20_out;
  wire [3:0] and_12_out;

  D_Flip_Flop d_ff_1 (.D(ns3), .clk(clk), .Q(state[3]), .reset(rst));  // open: Qn, preset
  D_Flip_Flop d_ff_2 (.D(ns4), .clk(clk), .Q(state[4]), .reset(rst));  // open: Qn, preset
  not not_1 (not_1_out, zero);
  D_Flip_Flop d_ff_3 (.D(ns0), .clk(clk), .Q(state[0]), .reset(rst));  // open: Qn, preset
  and and_1 (and_1_out, b17, zero);
  and and_2 (and_2_out, not_1_out, b18);
  or or_1 (pc_select[0], b21, b22, syns_out, alu_in2[0]);
  or or_2 (pc_select[1], b21, b14, b14);
  and and_3 (and_3_out, func[0], nf1, func[2]);
  and and_4 (and_4_out, nf0, nf2, func[1]);
  or or_3 (or_3_out, mul_enter, d_ff_6_q, div_enter);
  Counter #(.max('h4f)) counter_1 (
    .clr(or_3_out), .load(1'b0), .up(1'b1), .clk(clk), .carry(dive_done));  // open: count, D, Q
  D_Flip_Flop d_ff_4 (.D(ns1), .clk(clk), .Q(state[1]), .reset(rst));  // open: Qn, preset
  D_Flip_Flop d_ff_5 (.D(ns2), .clk(clk), .Q(state[2]), .reset(rst));  // open: Qn, preset
  or or_4 (pc_we, alu_in2[0], b14, b14, b21, and_1_out, and_2_out);
  or or_5 (alu_in1, alu_in2[0], b1);
  nor nor_1 (nor_1_out, func[2], func[4], func[5]);
  xnor xnor_1 (xnor_1_out, func[0], func[1]);
  or or_6 (or_6_out, and_3_out, and_4_out);
  D_Flip_Flop d_ff_6 (.D(dive_done), .clk(clk), .Q(d_ff_6_q));  // open: Qn, preset, reset
  and and_5 (and_5_out, nor_1_out, R_type);
  and and_6 (and_6_out, nf5, func[2], xnor_1_out);
  and and_7 (and_7_out, func[5], or_6_out);
  and and_8 (and_8_out, R_type, func[3]);
  or or_7 (write_data[1], b7, b22, b8);
  or or_8 (write_data[2], b20, b22, write_addr[2]);
  or or_9 (or_9_out, func[3], func[4]);
  Decoder #(.enable("false"), .select(5)) decoder_1 (
    .out0(alu_in2[0]), .out1(b1), .out2(b2), .out3(b3), .out4(b4), .out5(b5), .out6(b6), .out7(b7),
    .out8(b8), .out9(b9), .out10(b10), .out11(b11), .out12(b12), .out13(b13), .out14(b14),
    .out15(write_addr[2]), .out16(b16), .out17(b17), .out18(b18), .out19(b19), .out20(b20), .out21(b21),
    .out22(b22), .out23(syns_out), .out24(b24), .out25(b25), .out26(b26), .sel(state));  // open: out27, out28, out29, out30, out31
  or or_10 (write_addr[1], b7, b3, b22, b8);
  or or_11 (write_addr[0], b12, b20, b13, b3, b26);
  or or_12 (write_data[0], b26, b12, b8, b20);
  and and_9 (and_9_out, R_type, func[2], nf5);
  and and_10 (and_10_out, R_type, func[1], or_9_out);
  or or_13 (or_13_out, and_5_out, and_6_out, and_7_out, and_8_out);
  or or_14 (alu_in2[1], b24, b1, b13, b4, b9, b19, b25);
  or or_15 (and_12_out[3], and_9_out, and_5_out);
  and and_11 (and_12_out[2], R_type, func[2], func[5]);
  or or_16 (and_12_out[1], and_10_out, opcode[5]);
  and and_12 (and_12_out[0], R_type, or_13_out);
  or or_17 (mem_write, b10, b26);
  or or_18 (or_20_out[2], b4, b19, b16);
  or or_19 (or_20_out[1], b6, b5);
  Multiplexer #(.select(3), .width(4)) multiplexer_1 (
    .in0(4'b0000), .in1(and_12_out), .in2(4'b0011), .in3(4'b0010), .in4(4'b1001), .in5(4'b0001), .out(Aluop),
    .sel(or_20_out));  // open: in6, in7
  or or_20 (or_20_out[0], b16, b19, b6, b2);
  or or_21 (we_hilo, dive_done, dive_done);
  not not_2 (not_2_out, alu_in2[0]);
  and and_13 (s_in, not_2_out, syns_out, not_3_out);
  not not_3 (not_3_out, syns_in);
  and and_14 (and_14_out, func[1], func[5]);
  and and_15 (and_15_out, nf1, func[4]);
  not not_4 (not_4_out, dive_done);
  not not_5 (not_5_out, dive_done);
  or or_22 (or_22_out, func[2], and_14_out, and_15_out);
  and and_16 (and_16_out, opcode[2], n4);
  and and_17 (and_17_out, opcode[3], opcode[1], n0);
  and and_18 (and_18_out, opcode[1], n3);
  and and_19 (and_19_out, opcode[3], n1, n2);
  and and_20 (and_20_out, func[4], func[1], R_type);
  and and_21 (jr, R_type, nf1, func[3]);
  and and_22 (and_22_out, n1, n2, opcode[3]);
  and and_23 (and_23_out, R_type, nf5, nf4, nf2);
  and and_24 (div, R_type, not_4_out, b5);
  and and_25 (mfhi, R_type, func[4], n1);
  and and_26 (and_26_out, opcode[1], n3, n4, n5);
  and and_27 (mul_1, b6, not_5_out);
  and and_28 (and_28_out, opcode[1], n5);
  and and_29 (and_29_out, R_type, or_22_out);
  and and_30 (and_30_out, opcode[5], n3);
  and and_31 (and_31_out, opcode[3], n2, n1);
  and and_32 (and_32_out, opcode[3], n2);
  and and_33 (and_33_out, opcode[1], opcode[0]);
  and and_34 (div_enter, func[4], b1, R_type, func[3]);
  not not_6 (n0, opcode[0]);
  not not_7 (n1, opcode[1]);
  not not_8 (nf0, func[0]);
  and and_35 (and_35_out, opcode[0], opcode[5]);
  and and_36 (and_36_out, b6, dive_done);
  or or_23 (or_23_out, and_30_out, and_31_out);
  Comparator #(.mode("unsigned"), .width(6)) comparator_1 (.a(6'b100010), .b(opcode), .eq(exchange));  // open: gt, lt
  not not_9 (n2, opcode[2]);
  or or_24 (or_24_out, opcode[0], opcode[1], opcode[2], opcode[3], opcode[4], opcode[5]);
  not not_10 (nf1, func[1]);
  not not_11 (nf2, func[2]);
  or or_25 (or_25_out, and_16_out, and_17_out, jr);
  or or_26 (or_26_out, and_35_out, and_18_out, and_19_out, and_20_out);
  and and_37 (and_37_out, b9, and_22_out);
  or or_27 (or_27_out, jr, and_23_out, div, 1'b0, mfhi, and_26_out);
  and and_38 (and_38_out, b9, opcode[5]);
  and and_39 (and_39_out, b16, opcode[2], opcode[0], n4);
  or or_28 (or_28_out, 1'b0, and_28_out, and_29_out);
  and and_40 (mul_enter, b1, opcode[4]);
  and and_41 (and_41_out, b9, or_23_out);
  and and_42 (and_42_out, b16, opcode[2], n3, n0);
  and and_43 (and_43_out, b1, or_29_out);
  or or_29 (or_29_out, 1'b0, jr, mfhi, and_32_out, and_33_out, div_enter);
  not not_12 (n3, opcode[3]);
  not not_13 (n4, opcode[4]);
  not not_14 (R_type, or_24_out);
  not not_15 (nf3, func[3]);
  and and_44 (and_44_out, b1, n0, opcode[5]);
  and and_45 (and_45_out, b1, or_25_out);
  or or_30 (or_30_out, b19, mul_1, div_enter, mul_enter);
  and and_46 (and_46_out, b1, or_27_out);
  and and_47 (and_47_out, n1, b1, opcode[5], n0);
  and and_48 (and_48_out, b1, or_28_out);
  or or_31 (or_31_out, mul_enter, write_addr[2], and_36_out);
  not not_16 (n5, opcode[5]);
  not not_17 (nf4, func[4]);
  and and_49 (and_49_out, b1, or_26_out);
  and and_50 (and_50_out, n0, b1, opcode[5], n1);
  and and_51 (and_51_out, opcode[1], b1, n1, opcode[5], n0);
  not not_18 (nf5, func[5]);
  and and_52 (and_52_out, alu_in2[0], exchange);
  and and_53 (and_53_out, alu_in2[0], exchange);
  or or_32 (or_32_out, and_50_out, and_54_out);
  and and_54 (and_54_out, opcode[3], b1, opcode[5], n0);
  or or_33 (or_33_out, and_54_out, and_47_out, b4, mul_1);
  or or_34 (or_34_out, and_51_out, s_in, div);
  and and_55 (and_55_out, alu_in2[0], not_19_out);
  not not_19 (not_19_out, exchange);
  or or_35 (ns4, b25, and_52_out, and_44_out, b19, s_in, b16, and_45_out, b24);
  or or_36 (ns3, b24, and_53_out, b9, b11, write_addr[2], and_49_out, b25);
  or or_37 (ns2, or_30_out, write_addr[2], b11, s_in, and_37_out, and_46_out, or_32_out);
  or or_38 (ns1, b25, or_33_out, b2, and_38_out, and_39_out, and_48_out, or_31_out, s_in);
  or or_39 (ns0, or_34_out, b2, b4, and_36_out, b24, and_41_out, and_42_out, and_43_out, and_55_out);

  assign done = alu_in2[0];
  assign inst_we = alu_in2[0];

  // Other names for the same wires on the sheet: b0 = alu_in2[0]; b23 = syns_out; f0 = func[0]; f1 = func[1];
  //   f2 = func[2]; f3 = func[3]; f4 = func[4]; f5 = func[5]; mul_done = dive_done; op0 = opcode[0]; op1 = opcode[1];
  //   op2 = opcode[2]; op3 = opcode[3]; op4 = opcode[4]; op5 = opcode[5]; s0 = state[0]; s1 = state[1]; s2 = state[2];
  //   s3 = state[3]; s4 = state[4]; b15 = write_addr[2]; zero_in = zero
endmodule

module cpu (
  input  clk,
  input  rst,
  input  syns_in,
  input  [31:0] Dout,
  input  cpu_id,
  input  [31:0] DataMem,
  output InstDone,
  output mem_write,
  output [8:0] PC_out,
  output syns_out,
  output exchange,
  output [31:0] R1,
  output [31:0] R2,
  output [31:0] R3,
  output aluDone,
  output [31:0] R4,
  output [31:0] R5,
  output [31:0] R6,
  output [31:0] R7,
  output [31:0] R8,
  output [31:0] R9,
  output [31:0] WriteData,
  output [31:0] R10,
  output [31:0] R11,
  output [31:0] R12,
  output [31:0] R13,
  output [31:0] R14,
  output [31:0] R15,
  output [31:0] R16,
  output [8:0] address,
  output [31:0] R17,
  output [31:0] R18,
  output [31:0] R19,
  output [31:0] R20,
  output [31:0] R21,
  output [31:0] R22,
  output [31:0] R23,
  output [31:0] R24,
  output [31:0] R25,
  output [31:0] R26,
  output [31:0] R27,
  output [31:0] R28,
  output [31:0] R29,
  output [31:0] R30,
  output [31:0] R31,
  output [4:0] state
);

  wire alu_in1, comparator_1_lt, instr_we, pc_we, we_hilo, zero;
  wire [1:0] alu_in2, pc_select;
  wire [2:0] write_addr, write_data;
  wire [3:0] aluOp;
  wire [4:0] multiplexer_2_out, rd, rs, rt, shamt;
  wire [5:0] funct, opcode;
  wire [8:0] multiplexer_5_out;
  wire [15:0] immediate;
  wire [31:0] A, bit_extender_1_out, bit_extender_2_out, bit_extender_3_out, bit_extender_4_out, hi,
       Instruction_Register_q, lo, MemD, multiplexer_1_out, multiplexer_3_out, multiplexer_4_out, neg,
       Reg_file_dread0, Reg_file_dread1, res_high, res_low;
  wire [54:0] multiplexer_5_out_2;
  wire [63:0] adder_1_out, bit_extender_5_out, bit_extender_6_out, bit_extender_7_out;
  wire [63:9] ALUOut;

  Register #(.width(32)) Instruction_Register (
    .D(Dout), .en(instr_we), .clk(clk), .Q(Instruction_Register_q), .clr(rst));
  Control_Unit cu (
    .zero(zero), .opcode(opcode), .clk(clk), .rst(rst), .func(funct), .syns_in(syns_in), .inst_we(instr_we),
    .mem_write(mem_write), .pc_we(pc_we), .write_addr(write_addr), .alu_in2(alu_in2), .pc_select(pc_select),
    .write_data(write_data), .alu_in1(alu_in1), .Aluop(aluOp), .done(InstDone), .we_hilo(we_hilo),
    .syns_out(syns_out), .exchange(exchange), .state(state));
  Instruction_Decoder ID (
    .instruction(Instruction_Register_q), .immediate(immediate), .funct(funct), .shift(shamt), .rd(rd),
    .rt(rt), .rs(rs), .opcode(opcode));
  Register #(.width(32)) Memory_Data_Register (.D(DataMem), .en(1'b1), .clk(clk), .Q(MemD), .clr(rst));
  assign bit_extender_1_out = {{31{1'b0}}, cpu_id};  // Bit_Extender bit_extender_1
  assign bit_extender_2_out = {{23{1'b0}}, PC_out};  // Bit_Extender bit_extender_2
  Multiplexer #(.select(3), .width(32)) multiplexer_1 (
    .in0({ALUOut[31:9], address}), .in1(MemD), .in2(hi), .in3(lo), .in4(bit_extender_2_out), .in5(neg),
    .in6(bit_extender_1_out), .out(multiplexer_1_out), .sel(write_data));  // open: in7
  Multiplexer #(.select(3), .width(5)) multiplexer_2 (
    .in0({5{1'b0}}), .in1(rt), .in2(rs), .in3(rd), .in4({5{1'b1}}), .out(multiplexer_2_out), .sel(write_addr));  // open: in5, in6, in7
  regfile Reg_file (
    .clk(clk), .rst(rst), .Dwrite(multiplexer_1_out), .Awrite(multiplexer_2_out), .Aread0(rs), .Aread1(rt),
    .Dread0(Reg_file_dread0), .Dread1(Reg_file_dread1), .R1(R1), .R2(R2), .R3(R3), .R4(R4), .R5(R5), .R6(R6),
    .R7(R7), .R8(R8), .R9(R9), .R10(R10), .R11(R11), .R12(R12), .R13(R13), .R14(R14), .R15(R15), .R16(R16),
    .R17(R17), .R18(R18), .R19(R19), .R20(R20), .R21(R21), .R22(R22), .R23(R23), .R24(R24), .R25(R25),
    .R26(R26), .R27(R27), .R28(R28), .R29(R29), .R30(R30), .R31(R31));
  Register #(.width(32)) u_A (.D(Reg_file_dread0), .en(1'b1), .clk(clk), .Q(A), .clr(rst));
  Register #(.width(32)) B (.D(Reg_file_dread1), .en(1'b1), .clk(clk), .Q(WriteData), .clr(rst));
  assign bit_extender_3_out = {{16{immediate[15]}}, immediate};  // Bit_Extender bit_extender_3
  Multiplexer #(.select(2), .width(32)) multiplexer_3 (
    .in0(WriteData), .in1(32'h1), .in2(bit_extender_3_out), .out(multiplexer_3_out), .sel(alu_in2));  // open: in3
  assign bit_extender_4_out = {{23{1'b0}}, PC_out};  // Bit_Extender bit_extender_4
  Multiplexer #(.width(32)) multiplexer_4 (.in0(A), .in1(bit_extender_4_out), .out(multiplexer_4_out), .sel(alu_in1));
  Register #(.width(32)) u_LO (.D(res_low), .en(we_hilo), .clk(clk), .Q(lo), .clr(rst));
  Register #(.width(32)) u_HI (.D(res_high), .en(we_hilo), .clk(clk), .Q(hi), .clr(rst));
  ALU alu_circ (
    .a(multiplexer_4_out), .b(multiplexer_3_out), .rst(rst), .aluop(aluOp), .clk(clk), .res_low(res_low),
    .res_high(res_high), .done(aluDone));  // open: output_inc, output_inverted
  Register #(.width(9)) PC (.D(multiplexer_5_out), .en(pc_we), .clk(clk), .Q(PC_out), .clr(rst));
  assign bit_extender_5_out = {{55{PC_out[8]}}, PC_out};  // Bit_Extender bit_extender_5
  Multiplexer #(.select(2), .width(64)) multiplexer_5 (
    .in0(adder_1_out), .in1({res_high, res_low}), .in2(bit_extender_7_out), .in3(bit_extender_6_out),
    .out({multiplexer_5_out_2, multiplexer_5_out}), .sel(pc_select));
  Adder #(.width(64)) adder_1 (.a(bit_extender_5_out), .b(bit_extender_7_out), .out(adder_1_out));  // open: cin, cout
  assign bit_extender_6_out = {{32{A[31]}}, A};  // Bit_Extender bit_extender_6
  assign bit_extender_7_out = {{48{immediate[15]}}, immediate};  // Bit_Extender bit_extender_7
  Register #(.width(64)) u_ALUOut (.D({res_high, res_low}), .en(1'b1), .clk(clk), .Q({ALUOut, address}), .clr(rst));
  Comparator #(.width(64)) comparator_1 (
    .a({ALUOut, address}), .b({64{1'b0}}), .eq(zero), .lt(comparator_1_lt));  // open: gt
  assign neg = {{31{1'b0}}, comparator_1_lt};  // Bit_Extender bit_extender_8

  // Other names for the same wires on the sheet: ALUOut[8:0] = address; B[31:0] = WriteData; done = aluDone;
  //   ins_done = InstDone; PC[8:0] = PC_out
endmodule
